# Fritzing sketch skema (saved by Fritzing 0.9.3b)

parts:
  U1 = ESP32-38PinWide [part_number=ESP32-38PinWide]
  LCD2004-I2C1 = LCD2004-I2C
  SDS1 = SDS011 - dust sensor [part_number=1]

nets:
  VIN: U1.VIN, LCD2004-I2C1.VCC, SDS1.5v
  N1: U1.GPIO16, SDS1.RX
  N2: U1.GPIO17, SDS1.TX
  GND: U1.GND, SDS1.GND
  N3: U1.GPIO21, LCD2004-I2C1.SDA
  N4: U1.GPIO22, LCD2004-I2C1.SCL

custom parts:
  ESP32-38PinWide: Generic 38-Pin ESP32 with wide format (only access to one side of pins on a breadboard) based on Stephen Lilley's HiLetgo ESP-WROOM-32 ESP32 ESP-32S Development Board.
  LCD2004-I2C: A standard character display with 4x20 characters. Comes in many colors with LCM2004 IIC attached.
  SDS011 - dust sensor: The SDS 011 Sensor is a quite recent Air Quality Sensor developed by inovafit, a spin-off from the university of Jinan (in Shandong). With its size, it is probably one of the best sensor in terms of accuracy: While other sensors tend to focus on shrinking the sensor size, the SDS 011 has opted for a size tradeoff allowing it to use a larger fan. And the larger the fan, the better the quality.
